# Fritzing sketch CdSLED (saved by Fritzing 0.9.3b)

parts:
  Mod1 = Raspberry Pi Pico W
  LED1 = LED - 5mm [color="Red (633nm)" current=0.030 package="5 mm [THT]"]
  Mod2 = KY-018 Photoresistor Module [package="Breakout board"]

nets:
  N1: Mod1.pin_2, LED1.anode
  N2: Mod1.pin_3, Mod1.pin_33, LED1.cathode, Mod2.-
  N3: Mod1.pin_31, Mod2.S
  N4: Mod1.pin_36, Mod2.Vin

custom parts:
  Raspberry Pi Pico W: Raspberry Pi Pico W. Based around the RP2040 microcontroller the Pico W is a low cost microcontroller device bringing Raspberry Pi quality, cost, and easy of use to the microcontroller space. The areas marked KEEPOUT in pcb silkscreen should not have traces running through them to avoid shorts on a soldered in module!
  KY-018 Photoresistor Module: KY-018 Photoresistor module, used to measure light intensity. It can determine the presence or absence of light.
