# Fritzing sketch CdSNeopixel (saved by Fritzing 0.9.10b)
circuit board: 6.39161cm x 5.65702cm

parts:
  U1 = WS2812 RGB LED matrix 2x2
  Mod1 = Raspberry Pi Pico W
  Mod3 = KY-018 Photoresistor Module [package="Breakout board"]

nets:
  N1: U1.GND, Mod1.pin_33, Mod1.pin_38, Mod3.-
  VCC: U1.VCC, Mod1.pin_36, Mod3.Vin
  N2: U1.DIN, Mod1.pin_29
  N3: Mod1.pin_31, Mod3.S

custom parts:
  WS2812 RGB LED matrix 2x2: WS2812 matrix 2x2
  Raspberry Pi Pico W: Raspberry Pi Pico W. Based around the RP2040 microcontroller the Pico W is a low cost microcontroller device bringing Raspberry Pi quality, cost, and easy of use to the microcontroller space. The areas marked KEEPOUT in pcb silkscreen should not have traces running through them to avoid shorts on a soldered in module!
  KY-018 Photoresistor Module: KY-018 Photoresistor module, used to measure light intensity. It can determine the presence or absence of light.
