# Fritzing sketch smartFarm (saved by Fritzing 0.9.10b)
breadboards: 1

parts:
  Mod1 = Raspberry Pi Pico W
  U1 = L9110 H-bridge module [part_number="L9110 H-bridge"]
  TP1 = TP4056 [chip_label=TP4056 package="DIP (Dual Inline) [THT]"]
  LED1 = LED - 5mm [color="Red (633nm)" current=0.030 package="5 mm [THT]"]
  M1 = DC Motor [voltage_(max)=6V voltage_(min)=3V]
  M2 = DC Motor [voltage_(max)=6V voltage_(min)=3V]
  Grove1 = Grove OLED 128x96
  BAT1 = Battery Holders [package=lipo-1100mAh]
  R1 = PHOTOCELL [package=photocell-kit]
  부품1 = Soil Moisture Sensor
  R2 = Resistor [tolerance=±5% resistance=1k package="2512 [SMD]"]

nets:
  N1: Mod1.pin_2, LED1.anode
  GND: Mod1.pin_3, Mod1.pin_8, Mod1.pin_13, Mod1.pin_18, Mod1.pin_33, Mod1.pin_38, U1.B-IB, U1.GND, U1.A-IB, TP1.pin6, LED1.cathode, Grove1.GND, 부품1.GND, R2.Pin_1
  N2: Mod1.pin_7, U1.B-IA
  N3: Mod1.pin_12, U1.A-IA
  N4: Mod1.pin_21, Grove1.SDA
  N5: Mod1.pin_22, Grove1.SCL
  N6: Mod1.pin_31, 부품1.SIG
  N7: Mod1.pin_32, R1.P$2, R2.Pin_0
  N8: Mod1.pin_36, R1.P$1
  N9: Mod1.pin_40, U1.VCC, TP1.pin3
  N10: U1.MOTOR_A-A, M1.pin_2
  N11: U1.MOTOR_A-B, M1.pin_1
  N12: U1.MOTOR_B-A, M2.pin_2
  N13: U1.MOTOR_B-B, M2.pin_1
  N14: TP1.pin4, BAT1.+
  N15: TP1.pin5, BAT1.-
  VCC: Grove1.VCC, 부품1.VCC

custom parts:
  Raspberry Pi Pico W: Raspberry Pi Pico W. Based around the RP2040 microcontroller the Pico W is a low cost microcontroller device bringing Raspberry Pi quality, cost, and easy of use to the microcontroller space. The areas marked KEEPOUT in pcb silkscreen should not have traces running through them to avoid shorts on a soldered in module!
  TP4056: A DIP stand-in part for whatever IC you want. With 6 pins on a 300mil dual inline package (DIP) footprint.
